// Logisim project LogicDiagram.circ as structural Verilog: 1 circuit, main circuit main
module main (
  input  RW_Signal
);

  wire A_out, ADD, and_1_out, and_2_out, and_3_out, and_4_out, and_5_out, and_6_out, and_7_out, and_8_out,
       and_9_out, and_10_out, and_11_out, and_12_out, and_13_out, and_14_out, and_15_out, and_16_out,
       and_17_out, and_18_out, and_19_out, and_20_out, and_21_out, and_26_out, and_27_out, and_28_out,
       and_29_out, and_30_out, and_31_out, and_32_out, and_33_out, and_34_out, and_35_out, and_50_out,
       and_51_out, and_52_out, and_53_out, and_54_out, and_55_out, and_56_out, and_57_out, and_58_out,
       and_59_out, and_60_out, and_61_out, and_62_out, and_63_out, and_64_out, and_65_out, and_66_out,
       and_67_out, and_68_out, and_69_out, and_70_out, and_71_out, and_72_out, and_73_out, and_74_out,
       and_75_out, and_76_out, and_77_out, and_78_out, and_79_out, and_80_out, and_81_out, and_82_out,
       and_83_out, and_84_out, and_85_out, and_86_out, and_87_out, and_88_out, and_89_out, and_90_out,
       and_91_out, and_92_out, and_93_out, and_94_out, and_95_out, and_96_out, and_97_out, and_98_out,
       and_99_out, and_100_out, and_101_out, and_102_out, and_103_out, and_104_out, and_105_out, and_106_out,
       and_107_out, and_108_out, and_109_out, and_110_out, and_111_out, and_112_out, and_113_out,
       and_114_out, and_115_out, and_116_out, and_117_out, and_118_out, and_119_out, and_120_out,
       and_121_out, and_122_out, and_123_out, and_124_out, and_125_out, and_126_out, and_127_out,
       and_128_out, and_129_out, and_130_out, and_131_out, and_132_out, and_133_out, and_134_out,
       and_135_out, and_136_out, and_137_out, and_138_out, and_139_out, and_140_out, and_141_out,
       and_142_out, and_143_out, and_144_out, and_145_out, AND_Flag, B_out, Bit_Clock_carry, clock_1_out,
       clock_2_out, clock_3_out, Clock_In_out, Invert, nor_2_out, nor_4_out, nor_6_out, nor_8_out,
       nor_10_out, nor_12_out, nor_14_out, nor_16_out, nor_18_out, nor_20_out, nor_21_out, nor_22_out,
       nor_23_out, nor_24_out, nor_25_out, nor_26_out, not_1_out, not_2_out, not_3_out, not_4_out, not_5_out,
       not_6_out, not_7_out, not_8_out, not_9_out, not_10_out, not_11_out, not_12_out, not_13_out,
       not_14_out, not_15_out, not_16_out, not_17_out, not_18_out, not_19_out, not_20_out, not_21_out,
       not_22_out, not_23_out, not_24_out, not_25_out, not_26_out, not_27_out, not_28_out, not_29_out,
       not_30_out, not_31_out, not_32_out, not_33_out, not_34_out, not_35_out, not_36_out, not_37_out,
       not_38_out, not_39_out, not_40_out, not_41_out, not_42_out, not_43_out, not_44_out, not_45_out,
       not_46_out, not_47_out, not_48_out, not_49_out, not_50_out, not_51_out, not_52_out, not_53_out,
       or_1_out, or_2_out, or_3_out, or_4_out, OR_Flag, ram_2_dout, Reset, undriven_2, undriven_3,
       undriven_4, undriven_5, undriven_6, undriven_7, undriven_8, undriven_9, undriven_10, undriven_11,
       undriven_12, undriven_13, undriven_14, undriven_15, undriven_16, undriven_17, undriven_18,
       undriven_19, undriven_20, undriven_21, undriven_22, undriven_23, undriven_24, undriven_25,
       undriven_26, undriven_27, undriven_28, undriven_29, undriven_30, undriven_31, undriven_32,
       undriven_33, undriven_34, undriven_35, undriven_36, undriven_37, undriven_38, undriven_39,
       undriven_40, XOR_Flag;
  wire [2:0] Bit_Clock_q;
  wire [4:0] nor_1_out, nor_11_out, undriven;
  wire [5:0] Word_Clock_q;
  wire [31:0] or_6_out, undriven_41;

  not not_1 (not_1_out, undriven[0]);
  not not_2 (not_2_out, undriven[1]);
  not not_3 (not_3_out, undriven[2]);
  not not_4 (not_4_out, undriven[3]);
  not not_5 (not_5_out, undriven[4]);
  not not_6 (not_6_out, undriven[0]);
  not not_7 (not_7_out, undriven[1]);
  not not_8 (not_8_out, undriven[2]);
  not not_9 (not_9_out, undriven[3]);
  not not_10 (not_10_out, undriven[4]);
  and and_1 (and_1_out, undriven_2, undriven[0]);
  and and_2 (and_2_out, not_1_out, undriven_2);
  and and_3 (and_3_out, undriven_2, undriven[1]);
  and and_4 (and_4_out, not_2_out, undriven_2);
  and and_5 (and_5_out, undriven_2, undriven[2]);
  and and_6 (and_6_out, not_3_out, undriven_2);
  and and_7 (and_7_out, undriven_2, undriven[3]);
  and and_8 (and_8_out, not_4_out, undriven_2);
  and and_9 (and_9_out, undriven_2, undriven[4]);
  and and_10 (and_10_out, not_5_out, undriven_2);
  and and_11 (and_11_out, undriven_3, undriven[0]);
  and and_12 (and_12_out, not_6_out, undriven_3);
  and and_13 (and_13_out, undriven_3, undriven[1]);
  and and_14 (and_14_out, not_7_out, undriven_3);
  and and_15 (and_15_out, undriven_3, undriven[2]);
  and and_16 (and_16_out, not_8_out, undriven_3);
  and and_17 (and_17_out, undriven_3, undriven[3]);
  and and_18 (and_18_out, not_9_out, undriven_3);
  and and_19 (and_19_out, undriven_3, undriven[4]);
  and and_20 (and_20_out, not_10_out, undriven_3);
  nor nor_1 (nor_1_out[0], and_1_out, nor_2_out);
  nor nor_2 (nor_2_out, nor_1_out[0], and_2_out);
  nor nor_3 (nor_1_out[1], and_3_out, nor_4_out);
  nor nor_4 (nor_4_out, nor_1_out[1], and_4_out);
  nor nor_5 (nor_1_out[2], and_5_out, nor_6_out);
  nor nor_6 (nor_6_out, nor_1_out[2], and_6_out);
  nor nor_7 (nor_1_out[3], and_7_out, nor_8_out);
  nor nor_8 (nor_8_out, nor_1_out[3], and_8_out);
  nor nor_9 (nor_1_out[4], and_9_out, nor_10_out);
  nor nor_10 (nor_10_out, nor_1_out[4], and_10_out);
  nor nor_11 (nor_11_out[0], and_11_out, nor_12_out);
  nor nor_12 (nor_12_out, nor_11_out[0], and_12_out);
  nor nor_13 (nor_11_out[1], and_13_out, nor_14_out);
  nor nor_14 (nor_14_out, nor_11_out[1], and_14_out);
  nor nor_15 (nor_11_out[2], and_15_out, nor_16_out);
  nor nor_16 (nor_16_out, nor_11_out[2], and_16_out);
  nor nor_17 (nor_11_out[3], and_17_out, nor_18_out);
  nor nor_18 (nor_18_out, nor_11_out[3], and_18_out);
  nor nor_19 (nor_11_out[4], and_19_out, nor_20_out);
  nor nor_20 (nor_20_out, nor_11_out[4], and_20_out);
  // Probe on nor_1_out
  // Probe on nor_11_out
  Clock Clock_In (.out(Clock_In_out));
  buf or_1 (or_1_out, A_out);  // OR_Gate
  buf or_2 (or_2_out, B_out);  // OR_Gate
  Counter #(.max('h5), .width(3)) Bit_Clock (
    .clr(and_21_out), .clk(Clock_In_out), .carry(Bit_Clock_carry), .Q(Bit_Clock_q));  // open: load, up, count, D
  Counter #(.max('h3f), .width(6)) Word_Clock (
    .clk(and_21_out), .Q(Word_Clock_q));  // open: clr, load, up, count, D, carry
  and and_21 (and_21_out, Clock_In_out, Bit_Clock_carry);
  LED Bank_B (.in(nor_21_out));
  nor nor_21 (nor_21_out, or_1_out, nor_22_out);
  LED Bank_A (.in(nor_22_out));
  nor nor_22 (nor_22_out, nor_21_out, or_2_out);
  not not_11 (not_11_out, Bit_Clock_q[2]);
  not not_12 (not_12_out, Bit_Clock_q[1]);
  not not_13 (not_13_out, Bit_Clock_q[0]);
  Clock clock_1 (.out(clock_1_out));
  RAM #(.addrWidth(9), .dataWidth(32), .trigger("high")) ram_1 (
    .addr({Word_Clock_q, Bit_Clock_q}), .we(clock_2_out), .oe(1'b1));  // open: clk, din, dout
  Clock clock_2 (.out(clock_2_out));
  Button A (.out(A_out));
  Button B (.out(B_out));
  // AND_Gate and_22 has open pins: in0=not_13_out, in1=not_12_out, in2=not_11_out, out=open
  // AND_Gate and_23 has open pins: in0=Bit_Clock_q[0], in1=not_12_out, in2=not_11_out, out=open
  // AND_Gate and_24 has open pins: in0=not_13_out, in1=Bit_Clock_q[1], in2=not_11_out, out=open
  // AND_Gate and_25 has open pins: in0=Bit_Clock_q[0], in1=Bit_Clock_q[1], in2=not_11_out, out=open
  and and_26 (and_26_out, not_13_out, not_12_out, Bit_Clock_q[2]);
  RAM #(.addrWidth(3), .dataWidth(1), .trigger("high")) ram_2 (
    .addr(Bit_Clock_q), .we(clock_1_out), .oe(1'b1), .din(or_3_out), .dout(ram_2_dout));  // open: clk
  or or_3 (or_3_out, and_29_out, and_28_out);
  buf and_27 (and_27_out, undriven_4);  // AND_Gate
  DipSwitch #(.number(10)) Adress_Selector ();  // open: sw1, sw2, sw3, sw4, sw5, sw6, sw7, sw8, sw9, sw10
  Clock clock_3 (.out(clock_3_out));
  not not_14 (not_14_out, clock_3_out);
  and and_28 (and_28_out, ram_2_dout, not_15_out);
  not not_15 (not_15_out, and_27_out);
  buf and_29 (and_29_out, and_27_out);  // AND_Gate
  and and_30 (and_30_out, not_14_out, and_26_out);
  or or_4 (or_4_out, Reset, nor_26_out);
  DipSwitch #(.number(5)) Data ();  // open: sw1, sw2, sw3, sw4, sw5
  and and_31 (and_31_out, and_30_out, or_4_out);
  not not_16 (not_16_out, or_4_out);
  and and_32 (and_32_out, not_16_out, and_30_out);
  nor nor_23 (nor_23_out, and_31_out, nor_24_out);
  nor nor_24 (nor_24_out, nor_23_out, and_32_out);
  not not_17 (not_17_out, and_30_out);
  and and_33 (and_33_out, not_17_out, nor_23_out);
  and and_34 (and_34_out, nor_24_out, not_17_out);
  nor nor_25 (nor_25_out, and_33_out, nor_26_out);
  nor nor_26 (nor_26_out, nor_25_out, and_34_out);
  not not_18 (not_18_out, undriven_8);
  not not_19 (not_19_out, undriven_7);
  not not_20 (not_20_out, undriven_6);
  not not_21 (not_21_out, undriven_5);
  and and_35 (and_35_out, undriven_5, not_20_out, not_19_out, not_18_out);
  and and_36 (ADD, not_21_out, undriven_6, not_19_out, not_18_out);
  and and_37 (OR_Flag, undriven_5, undriven_6, not_19_out, not_18_out);
  and and_38 (XOR_Flag, not_21_out, not_20_out, undriven_7, not_18_out);
  and and_39 (AND_Flag, undriven_5, not_20_out, undriven_7, not_18_out);
  and and_40 (Invert, not_21_out, undriven_6, undriven_7, not_18_out);
  // AND_Gate and_41 has open pins: in0=undriven_5, in1=undriven_6, in2=undriven_7, in3=not_18_out, out=open
  // AND_Gate and_42 has open pins: in0=not_21_out, in1=not_20_out, in2=not_19_out, in3=undriven_8, out=open
  // AND_Gate and_43 has open pins: in0=undriven_5, in1=not_20_out, in2=not_19_out, in3=undriven_8, out=open
  // AND_Gate and_44 has open pins: in0=not_21_out, in1=undriven_6, in2=not_19_out, in3=undriven_8, out=open
  // AND_Gate and_45 has open pins: in0=undriven_5, in1=undriven_6, in2=not_19_out, in3=undriven_8, out=open
  // AND_Gate and_46 has open pins: in0=not_21_out, in1=not_20_out, in2=undriven_7, in3=undriven_8, out=open
  // AND_Gate and_47 has open pins: in0=undriven_5, in1=not_20_out, in2=undriven_7, in3=undriven_8, out=open
  // AND_Gate and_48 has open pins: in0=not_21_out, in1=undriven_6, in2=undriven_7, in3=undriven_8, out=open
  // AND_Gate and_49 has open pins: in0=undriven_5, in1=undriven_6, in2=undriven_7, in3=undriven_8, out=open
  // OR_Gate or_5 has open pins: in0=ADD, in1=OR_Flag, in2=XOR_Flag, in3=AND_Flag, in4=Invert, out=open
  or or_6 (or_6_out[0], and_83_out, and_82_out);
  and and_50 (and_50_out, RW_Signal, undriven_39);
  or or_7 (or_6_out[1], and_85_out, and_84_out);
  and and_51 (and_51_out, RW_Signal, undriven_38);
  or or_8 (or_6_out[2], and_87_out, and_86_out);
  and and_52 (and_52_out, RW_Signal, undriven_37);
  or or_9 (or_6_out[3], and_89_out, and_88_out);
  and and_53 (and_53_out, RW_Signal, undriven_36);
  or or_10 (or_6_out[4], and_91_out, and_90_out);
  and and_54 (and_54_out, RW_Signal, undriven_35);
  or or_11 (or_6_out[5], and_93_out, and_92_out);
  and and_55 (and_55_out, RW_Signal, undriven_34);
  or or_12 (or_6_out[6], and_95_out, and_94_out);
  and and_56 (and_56_out, RW_Signal, undriven_33);
  or or_13 (or_6_out[7], and_97_out, and_96_out);
  and and_57 (and_57_out, RW_Signal, undriven_32);
  or or_14 (or_6_out[8], and_99_out, and_98_out);
  and and_58 (and_58_out, RW_Signal, undriven_31);
  or or_15 (or_6_out[9], and_101_out, and_100_out);
  and and_59 (and_59_out, RW_Signal, undriven_30);
  or or_16 (or_6_out[10], and_103_out, and_102_out);
  and and_60 (and_60_out, RW_Signal, undriven_29);
  or or_17 (or_6_out[11], and_105_out, and_104_out);
  and and_61 (and_61_out, RW_Signal, undriven_28);
  or or_18 (or_6_out[12], and_107_out, and_106_out);
  and and_62 (and_62_out, RW_Signal, undriven_27);
  or or_19 (or_6_out[13], and_109_out, and_108_out);
  and and_63 (and_63_out, RW_Signal, undriven_26);
  or or_20 (or_6_out[14], and_111_out, and_110_out);
  and and_64 (and_64_out, RW_Signal, undriven_25);
  or or_21 (or_6_out[15], and_113_out, and_112_out);
  and and_65 (and_65_out, RW_Signal, undriven_24);
  or or_22 (or_6_out[16], and_115_out, and_114_out);
  and and_66 (and_66_out, RW_Signal, undriven_24);
  or or_23 (or_6_out[17], and_117_out, and_116_out);
  and and_67 (and_67_out, RW_Signal, undriven_23);
  or or_24 (or_6_out[18], and_119_out, and_118_out);
  and and_68 (and_68_out, RW_Signal, undriven_22);
  or or_25 (or_6_out[19], and_121_out, and_120_out);
  and and_69 (and_69_out, RW_Signal, undriven_21);
  or or_26 (or_6_out[20], and_123_out, and_122_out);
  and and_70 (and_70_out, RW_Signal, undriven_20);
  or or_27 (or_6_out[21], and_125_out, and_124_out);
  and and_71 (and_71_out, RW_Signal, undriven_19);
  or or_28 (or_6_out[22], and_127_out, and_126_out);
  and and_72 (and_72_out, RW_Signal, undriven_18);
  or or_29 (or_6_out[23], and_129_out, and_128_out);
  and and_73 (and_73_out, RW_Signal, undriven_17);
  or or_30 (or_6_out[24], and_131_out, and_130_out);
  and and_74 (and_74_out, RW_Signal, undriven_16);
  or or_31 (or_6_out[25], and_133_out, and_132_out);
  and and_75 (and_75_out, RW_Signal, undriven_15);
  or or_32 (or_6_out[26], and_135_out, and_134_out);
  and and_76 (and_76_out, RW_Signal, undriven_14);
  or or_33 (or_6_out[27], and_137_out, and_136_out);
  and and_77 (and_77_out, RW_Signal, undriven_13);
  or or_34 (or_6_out[28], and_139_out, and_138_out);
  and and_78 (and_78_out, RW_Signal, undriven_12);
  or or_35 (or_6_out[29], and_141_out, and_140_out);
  and and_79 (and_79_out, RW_Signal, undriven_11);
  or or_36 (or_6_out[30], and_143_out, and_142_out);
  and and_80 (and_80_out, RW_Signal, undriven_10);
  or or_37 (or_6_out[31], and_145_out, and_144_out);
  and and_81 (and_81_out, RW_Signal, undriven_9);
  and and_82 (and_82_out, undriven_41[0], not_22_out);
  not not_22 (not_22_out, and_50_out);
  and and_83 (and_83_out, and_50_out, undriven_40);
  and and_84 (and_84_out, undriven_41[1], not_23_out);
  not not_23 (not_23_out, and_51_out);
  and and_85 (and_85_out, and_51_out, undriven_40);
  and and_86 (and_86_out, undriven_41[2], not_24_out);
  not not_24 (not_24_out, and_52_out);
  and and_87 (and_87_out, and_52_out, undriven_40);
  and and_88 (and_88_out, undriven_41[3], not_25_out);
  not not_25 (not_25_out, and_53_out);
  and and_89 (and_89_out, and_53_out, undriven_40);
  and and_90 (and_90_out, undriven_41[4], not_26_out);
  not not_26 (not_26_out, and_54_out);
  and and_91 (and_91_out, and_54_out, undriven_40);
  and and_92 (and_92_out, undriven_41[5], not_27_out);
  not not_27 (not_27_out, and_55_out);
  and and_93 (and_93_out, and_55_out, undriven_40);
  and and_94 (and_94_out, undriven_41[6], not_28_out);
  not not_28 (not_28_out, and_56_out);
  and and_95 (and_95_out, and_56_out, undriven_40);
  and and_96 (and_96_out, undriven_41[7], not_29_out);
  not not_29 (not_29_out, and_57_out);
  and and_97 (and_97_out, and_57_out, undriven_40);
  and and_98 (and_98_out, undriven_41[8], not_30_out);
  not not_30 (not_30_out, and_58_out);
  and and_99 (and_99_out, and_58_out, undriven_40);
  and and_100 (and_100_out, undriven_41[9], not_31_out);
  not not_31 (not_31_out, and_59_out);
  and and_101 (and_101_out, and_59_out, undriven_40);
  and and_102 (and_102_out, undriven_41[10], not_32_out);
  not not_32 (not_32_out, and_60_out);
  and and_103 (and_103_out, and_60_out, undriven_40);
  and and_104 (and_104_out, undriven_41[11], not_33_out);
  not not_33 (not_33_out, and_61_out);
  and and_105 (and_105_out, and_61_out, undriven_40);
  and and_106 (and_106_out, undriven_41[12], not_34_out);
  not not_34 (not_34_out, and_62_out);
  and and_107 (and_107_out, and_62_out, undriven_40);
  and and_108 (and_108_out, undriven_41[13], not_35_out);
  not not_35 (not_35_out, and_63_out);
  buf and_109 (and_109_out, and_63_out);  // AND_Gate
  and and_110 (and_110_out, undriven_41[14], not_36_out);
  not not_36 (not_36_out, and_64_out);
  and and_111 (and_111_out, and_64_out, undriven_40);
  and and_112 (and_112_out, undriven_41[15], not_37_out);
  not not_37 (not_37_out, and_65_out);
  and and_113 (and_113_out, and_65_out, undriven_40);
  and and_114 (and_114_out, undriven_41[16], not_38_out);
  not not_38 (not_38_out, and_66_out);
  and and_115 (and_115_out, and_66_out, undriven_40);
  and and_116 (and_116_out, undriven_41[17], not_39_out);
  not not_39 (not_39_out, and_67_out);
  and and_117 (and_117_out, and_67_out, undriven_40);
  and and_118 (and_118_out, undriven_41[18], not_40_out);
  not not_40 (not_40_out, and_68_out);
  and and_119 (and_119_out, and_68_out, undriven_40);
  and and_120 (and_120_out, undriven_41[19], not_41_out);
  not not_41 (not_41_out, and_69_out);
  and and_121 (and_121_out, and_69_out, undriven_40);
  and and_122 (and_122_out, undriven_41[20], not_42_out);
  not not_42 (not_42_out, and_70_out);
  and and_123 (and_123_out, and_70_out, undriven_40);
  and and_124 (and_124_out, undriven_41[21], not_43_out);
  not not_43 (not_43_out, and_71_out);
  and and_125 (and_125_out, and_71_out, undriven_40);
  and and_126 (and_126_out, undriven_41[22], not_44_out);
  not not_44 (not_44_out, and_72_out);
  and and_127 (and_127_out, and_72_out, undriven_40);
  and and_128 (and_128_out, undriven_41[23], not_45_out);
  not not_45 (not_45_out, and_73_out);
  and and_129 (and_129_out, and_73_out, undriven_40);
  and and_130 (and_130_out, undriven_41[24], not_46_out);
  not not_46 (not_46_out, and_74_out);
  and and_131 (and_131_out, and_74_out, undriven_40);
  and and_132 (and_132_out, undriven_41[25], not_47_out);
  not not_47 (not_47_out, and_75_out);
  and and_133 (and_133_out, and_75_out, undriven_40);
  and and_134 (and_134_out, undriven_41[26], not_48_out);
  not not_48 (not_48_out, and_76_out);
  and and_135 (and_135_out, and_76_out, undriven_40);
  and and_136 (and_136_out, undriven_41[27], not_49_out);
  not not_49 (not_49_out, and_77_out);
  and and_137 (and_137_out, and_77_out, undriven_40);
  and and_138 (and_138_out, undriven_41[28], not_50_out);
  not not_50 (not_50_out, and_78_out);
  and and_139 (and_139_out, and_78_out, undriven_40);
  and and_140 (and_140_out, undriven_41[29], not_51_out);
  not not_51 (not_51_out, and_79_out);
  and and_141 (and_141_out, and_79_out, undriven_40);
  and and_142 (and_142_out, undriven_41[30], not_52_out);
  not not_52 (not_52_out, and_80_out);
  and and_143 (and_143_out, and_80_out, undriven_40);
  and and_144 (and_144_out, undriven_41[31], not_53_out);
  not not_53 (not_53_out, and_81_out);
  and and_145 (and_145_out, and_81_out, undriven_40);

  // Notes on the sheet:
  //   Bank Slector
  //   Nop Instrucion
endmodule
